# Fritzing sketch rpi3_breadboard_schematics (saved by Fritzing 0.9.3b)

parts:
  LPD8806_RGB_LED_Strip3 = LPD8806 RGB LED Strip
  Raspberry_Pi_2 = Raspberry Pi 3 [part_number=RPI-3-V1.2]
  GY2 = MPU-6050 Board GY-521 [form="♀ (female)" package=THT]
  Power_plug1 = Power plug

nets:
  GND: LPD8806_RGB_LED_Strip3.GND, Power_plug1.GND
  N1: LPD8806_RGB_LED_Strip3.DI, Raspberry_Pi_2.GPIO10
  N2: LPD8806_RGB_LED_Strip3.CI, Raspberry_Pi_2.GPIO11
  +5V: LPD8806_RGB_LED_Strip3.+5V, Power_plug1.VCC
  N3: Raspberry_Pi_2.GPIO2, GY2.pin4
  N4: Raspberry_Pi_2.GPIO3, GY2.pin3
  N5: Raspberry_Pi_2.GND, GY2.pin2
  N6: Raspberry_Pi_2.5V, GY2.pin1

custom parts:
  LPD8806 RGB LED Strip: Digitally addressable RGB LED strip
  MPU-6050 Board GY-521: Acelerometro y Giroscopio MPU-6050 Board GY-521
