# Fritzing sketch rpi3_breadboard_schematics (saved by Fritzing 0.9.3b)
circuit board: 7.91634cm x 5.57388cm
breadboards: 1

parts:
  Raspberry_Pi_1 = Raspberry Pi 3 [part_number=RPI-3-V1.2]
  S_GREEN = Pushbutton [package="[THT]"]
  LED_GREEN = smd LED [color="Green (555nm)" package="1206 [SMD]"]
  LED_RED = smd LED [color="Red (633nm)" package="1206 [SMD]"]
  LED_BLUE = smd LED [color="Blue (430nm)" package="1206 [SMD]"]
  S_BLUE = Pushbutton [package="[THT]"]
  S_YELLOW = Pushbutton [package="[THT]"]
  BUZZER = Piezo Speaker
  R_BUZZER = Resistor [tolerance=±5% resistance=100 package=THT]
  LED_YELLOW = smd LED [color="Yellow (585nm)" package="1206 [SMD]"]
  R_L_BLUE = Resistor [tolerance=±5% resistance=470 package=THT]
  R_L_RED = Resistor [tolerance=±5% resistance=470 package=THT]
  R_L_YELLOW = Resistor [tolerance=±5% resistance=470 package=THT]
  S_RED = Pushbutton [package="[THT]"]
  R_S_GREEN = Resistor [tolerance=±5% resistance=10k package=THT]
  R_S_RED = Resistor [tolerance=±5% resistance=10k package=THT]
  S_TOGGLE = Pushbutton [package="[THT]"]
  R_S_TOGGLE = Resistor [tolerance=±5% resistance=10k package=THT]
  R_L_GREEN = Resistor [tolerance=±5% resistance=470 package=THT]
  R_S_BLUE = Resistor [tolerance=±5% resistance=10k package=THT]
  R_S_YELLOW = Resistor [tolerance=±5% resistance=10k package=THT]

nets:
  N1: Raspberry_Pi_1.GPIO5, R_L_GREEN.Pin_0
  N2: Raspberry_Pi_1.GPIO6, R_L_RED.Pin_0
  N3: Raspberry_Pi_1.GPIO19, R_L_BLUE.Pin_0
  N4: Raspberry_Pi_1.GPIO26, R_L_YELLOW.Pin_0
  N5: Raspberry_Pi_1.GPIO21, S_YELLOW.Pin_3, S_YELLOW.Pin_4, R_S_YELLOW.Pin_1
  N6: Raspberry_Pi_1.GPIO20, S_BLUE.Pin_3, S_BLUE.Pin_4, R_S_BLUE.Pin_1
  N7: Raspberry_Pi_1.GPIO16, S_RED.Pin_3, S_RED.Pin_4, R_S_RED.Pin_1
  N8: Raspberry_Pi_1.GPIO12, S_GREEN.Pin_3, S_GREEN.Pin_4, R_S_GREEN.Pin_1
  N9: Raspberry_Pi_1.GPIO25, S_TOGGLE.Pin_3, S_TOGGLE.Pin_4, R_S_TOGGLE.Pin_1
  N10: Raspberry_Pi_1.GPIO18, R_BUZZER.Pin_0
  N11: Raspberry_Pi_1.GND, S_GREEN.Pin_1, S_GREEN.Pin_2, LED_GREEN.cathode, LED_RED.cathode, LED_BLUE.cathode, S_BLUE.Pin_1, S_BLUE.Pin_2, S_YELLOW.Pin_1, S_YELLOW.Pin_2, BUZZER.pin1, LED_YELLOW.cathode, S_RED.Pin_1, S_RED.Pin_2, S_TOGGLE.Pin_1, S_TOGGLE.Pin_2
  N12: Raspberry_Pi_1.5V, R_S_GREEN.Pin_0, R_S_RED.Pin_0, R_S_TOGGLE.Pin_0, R_S_BLUE.Pin_0, R_S_YELLOW.Pin_0
  N13: LED_GREEN.anode, R_L_GREEN.Pin_1
  N14: LED_RED.anode, R_L_RED.Pin_1
  N15: LED_BLUE.anode, R_L_BLUE.Pin_1
  N16: BUZZER.pin2, R_BUZZER.Pin_1
  N17: LED_YELLOW.anode, R_L_YELLOW.Pin_1
